// Logisim project circuitoalarme.circ as structural Verilog: 2 circuits, main circuit main
module main (
  input  in_1
);
endmodule

module Circuito_alarme (
  input  A,
  input  B,
  input  C
);

  wire and_1_out, or_1_out;

  or or_1 (or_1_out, A, B);
  and and_1 (and_1_out, C, or_1_out);
  LED led_1 (.in(and_1_out));
endmodule
